# Fritzing sketch schematic (saved by Fritzing 0.9.4)
breadboards: 1

parts:
  Parça1 = Arduino Nano (Rev3.0) (ICSP)
  BAT1 = Battery Holders [package=battery-aa]
  Parça2 = Bluetooth HC-05 Macho
  R1 = Resistor [tolerance=±5% resistance=10k package="2010 [SMD]"]

nets:
  N1: Parça1.D1/TX, Parça2.RXD
  N2: Parça1.D0/RX, Parça2.TXD
  GND: Parça1.GND, BAT1.-, Parça2.GND, R1.Pin_1
  5V: Parça1.5V, Parça2.VCC
  N3: Parça1.A0, BAT1.+, R1.Pin_0
